// Logisim project hw6.circ as structural Verilog: 1 circuit, main circuit main
module main (
  input  _1_s_Place,
  input  _2_s_Place,
  input  _4_s_Place,
  output out_4
);

  wire and_1_out, and_2_out, not_1_out, not_2_out, or_1_out;

  or or_1 (or_1_out, _4_s_Place, _2_s_Place);
  not not_1 (not_1_out, _1_s_Place);
  not not_2 (not_2_out, or_1_out);
  and and_1 (and_1_out, or_1_out, not_1_out);
  and and_2 (and_2_out, _1_s_Place, not_2_out);
  or or_2 (out_4, and_1_out, and_2_out);

  // Other names for the same wires on the sheet: _1_s = _1_s_Place; _2_s = _2_s_Place; _4_s = _4_s_Place
endmodule
