// Logisim project P1.circ as structural Verilog: 7 circuits, main circuit main
module main (
  input  in_1,
  input  in_2,
  output out_3,
  output [7:0] out_4,
  output [7:0] out_5
);

  NAND nand_1 (.in_1(in_1), .in_2(in_2), .out_3(out_3));
  AddMachine addmachine_1 (.out_1(out_4), .out_2(out_5));
endmodule

module NAND (
  input  in_1,
  input  in_2,
  output out_3
);

  wire and_1_out;

  not not_1 (out_3, and_1_out);
  and and_1 (and_1_out, in_1, in_2);
endmodule

module NOR (
  input  in_1,
  input  in_2,
  output out_3
);

  wire or_1_out;

  or or_1 (or_1_out, in_1, in_2);
  not not_1 (out_3, or_1_out);
endmodule

module XOR (
  input  in_1,
  input  in_2,
  output out_3
);

  wire and_1_out, and_2_out, not_1_out, not_2_out;

  not not_1 (not_1_out, in_1);
  not not_2 (not_2_out, in_2);
  and and_1 (and_1_out, not_1_out, in_2);
  and and_2 (and_2_out, in_1, not_2_out);
  or or_1 (out_3, and_1_out, and_2_out);
endmodule

module _2_to_1_MUX (
  input  in_1,
  input  in_2,
  input  in_3,
  output out_4
);

  wire and_1_out, and_2_out, not_1_out;

  not not_1 (not_1_out, in_2);
  and and_1 (and_1_out, in_1, not_1_out);
  and and_2 (and_2_out, in_2, in_3);
  or or_1 (out_4, and_1_out, and_2_out);
endmodule

module _4_to_1_MUX (
  input  A,
  input  S0,
  input  B,
  input  S1,
  input  C,
  input  D,
  output out_7
);

  wire n2_to_1_mux_1_out_4, n2_to_1_mux_2_out_4;

  _2_to_1_MUX u_2_to_1_mux_1 (.in_1(A), .in_2(S0), .in_3(B), .out_4(n2_to_1_mux_1_out_4));
  _2_to_1_MUX u_2_to_1_mux_2 (.in_1(C), .in_2(S0), .in_3(D), .out_4(n2_to_1_mux_2_out_4));
  _2_to_1_MUX u_2_to_1_mux_3 (.in_1(n2_to_1_mux_1_out_4), .in_2(S1), .in_3(n2_to_1_mux_2_out_4), .out_4(out_7));

  // Other names for the same wires on the sheet: T0 = S1
endmodule

module AddMachine (
  output [7:0] out_1,
  output [7:0] out_2
);

  wire clock_1_out;

  Adder adder_1 (.a(8'h1), .b(out_2), .out(out_1));  // open: cin, cout
  Clock clock_1 (.out(clock_1_out));
  Register register_1 (.D(out_1), .Q(out_2), .clk(clock_1_out));  // open: en, clr
endmodule
