// Logisim project A.circ as structural Verilog: 5 circuits, main circuit Ex1
module main (
  input  [15:0] A,
  input  [3:0] B,
  output [15:0] out_3
);

  rotr rotr_1 (.A(A), .B(B), .out_3(out_3));
endmodule

module Ex1 (
  input  [7:0] Input,
  output [7:0] Out2,
  output Out1
);

  and and_1 (Out1, Input[0], Input[7]);
  not not_1 (Out2[7], Input[7]);

  assign Out2[6:0] = Input[6:0];

  // Other names for the same wires on the sheet: M[5:0] = Input[6:1]
endmodule

module rotr (
  input  [15:0] A,
  input  [3:0] B,
  output [15:0] out_3
);

  wire [3:0] roto_1_out_4, roto_2_out_4, roto_3_out_4, roto_4_out_4, roto_5_out_4, roto_6_out_4,
       roto_7_out_4, roto_8_out_4, roto_9_out_4, roto_10_out_4, roto_11_out_4, roto_12_out_4, roto_13_out_4,
       roto_14_out_4, roto_15_out_4;
  wire [15:0] roto_1_out, roto_2_out, roto_3_out, roto_4_out, roto_5_out, roto_6_out, roto_7_out, roto_8_out,
       roto_9_out, roto_10_out, roto_11_out, roto_12_out, roto_13_out, roto_14_out, roto_15_out;

  roto roto_1 (.In(roto_2_out), .in_2(roto_2_out_4), .Out(roto_1_out), .out_4(roto_1_out_4));
  roto roto_2 (.In(A), .in_2(B), .Out(roto_2_out), .out_4(roto_2_out_4));
  roto roto_3 (.In(roto_4_out), .in_2(roto_4_out_4), .Out(roto_3_out), .out_4(roto_3_out_4));
  roto roto_4 (.In(roto_1_out), .in_2(roto_1_out_4), .Out(roto_4_out), .out_4(roto_4_out_4));
  roto roto_5 (.In(roto_6_out), .in_2(roto_6_out_4), .Out(roto_5_out), .out_4(roto_5_out_4));
  roto roto_6 (.In(roto_3_out), .in_2(roto_3_out_4), .Out(roto_6_out), .out_4(roto_6_out_4));
  roto roto_7 (.In(roto_5_out), .in_2(roto_5_out_4), .Out(roto_7_out), .out_4(roto_7_out_4));
  roto roto_8 (.In(roto_7_out), .in_2(roto_7_out_4), .Out(roto_8_out), .out_4(roto_8_out_4));
  roto roto_9 (.In(roto_8_out), .in_2(roto_8_out_4), .Out(roto_9_out), .out_4(roto_9_out_4));
  roto roto_10 (.In(roto_9_out), .in_2(roto_9_out_4), .Out(roto_10_out), .out_4(roto_10_out_4));
  roto roto_11 (.In(roto_12_out), .in_2(roto_12_out_4), .Out(roto_11_out), .out_4(roto_11_out_4));
  roto roto_12 (.In(roto_10_out), .in_2(roto_10_out_4), .Out(roto_12_out), .out_4(roto_12_out_4));
  roto roto_13 (.In(roto_14_out), .in_2(roto_14_out_4), .Out(roto_13_out), .out_4(roto_13_out_4));
  roto roto_14 (.In(roto_11_out), .in_2(roto_11_out_4), .Out(roto_14_out), .out_4(roto_14_out_4));
  roto roto_15 (.In(roto_13_out), .in_2(roto_13_out_4), .Out(roto_15_out), .out_4(roto_15_out_4));
  roto roto_16 (.In(roto_15_out), .in_2(roto_15_out_4), .Out(out_3));  // open: out_4
endmodule

module roto (
  input  [15:0] In,
  input  [3:0] in_2,
  output [15:0] Out,
  output [3:0] out_4
);

  wire or_1_out;
  wire [3:0] subtractor_1_out;

  Multiplexer #(.width(16)) multiplexer_1 (.in0(In), .in1({In[0], In[15:1]}), .out(Out), .sel(or_1_out));  // open: en
  or or_1 (or_1_out, in_2[0], in_2[1], in_2[2], in_2[3]);
  Subtractor #(.width(4)) subtractor_1 (.a(in_2), .b(4'b0001), .out(subtractor_1_out));  // open: bin, bout
  Multiplexer #(.width(4)) multiplexer_2 (
    .in0(4'b0000), .in1(subtractor_1_out), .out(out_4), .sel(or_1_out));  // open: en

  // Other names for the same wires on the sheet: S = In[0]; A[3:0] = in_2
endmodule

module Fib (
  input  [3:0] in_1,
  output [10:0] out_2
);

  wire C, i;
  wire [3:0] counter_1_q;
  wire [10:0] adder_1_out, register_2_q;

  Clock clock_1 (.out(C));
  Counter #(.width(4), .max('hf)) counter_1 (.count(i), .Q(counter_1_q), .clk(C));  // open: load, D, carry, clr
  Comparator #(.width(4), .mode("unsigned")) comparator_1 (.a(counter_1_q), .b(in_1), .lt(i));  // open: gt, eq
  Register #(.width(11)) register_1 (.D(register_2_q), .en(i), .Q(out_2), .clk(C));  // open: clr
  Register #(.width(11)) register_2 (.D(adder_1_out), .en(i), .Q(register_2_q), .clk(C));  // open: clr
  Adder #(.width(11)) adder_1 (.a(out_2), .b(register_2_q), .out(adder_1_out));  // open: cin, cout
  // Probe on register_2_q
  // Probe on out_2
endmodule
