// Logisim project alu.circ as structural Verilog: 13 circuits, main circuit main
module main (
  input  [15:0] X,
  input  [15:0] Y,
  input  [3:0] switch__S,
  output signed_overflow,
  output [15:0] result,
  output equal
);

  wire add_1_overflow, decoder_1_out6, decoder_1_out7, or_2_out, or_3_out, sub_1_overflow;
  wire [15:0] add_1_out, and_1_out, bc_1_out, ffo_1_out, lui_1_out, or_1_out, sllv_1_out, slt_1_out,
       srav_1_out, srlv_1_out, sub_1_out, zb_1_out;

  \and  and_1 (.X(X), .Y(Y), .out(and_1_out));
  \or  or_1 (.X(X), .Y(Y), .out(or_1_out));
  slt slt_1 (.X(X), .Y(Y), .out(slt_1_out));
  sllv sllv_1 (.X(X), .Y(Y), .out(sllv_1_out));
  srlv srlv_1 (.X(X), .Y(Y), .out(srlv_1_out));
  srav srav_1 (.X(X), .Y(Y), .out(srav_1_out));
  add add_1 (.X(X), .Y(Y), .out(add_1_out), .overflow(add_1_overflow));
  sub sub_1 (.X(X), .Y(Y), .out(sub_1_out), .overflow(sub_1_overflow));
  ffo ffo_1 (.X(X), .out(ffo_1_out));
  zb zb_1 (.X(X), .out(zb_1_out));
  bc bc_1 (.X(X), .out(bc_1_out));
  lui lui_1 (.X(Y), .out(lui_1_out));
  Comparator #(.width(16)) comparator_1 (.a(X), .b(Y), .eq(equal));  // open: gt, lt
  Decoder #(.select(4), .enable("false")) decoder_1 (
    .out6(decoder_1_out6), .out7(decoder_1_out7), .sel(switch__S));  // open: out0, out1, out2, out3, out4, out5, out8, out9, out10, out11, out12, out13, out14, out15
  Multiplexer #(.select(4), .width(16), .enable("false")) multiplexer_1 (
    .in0(and_1_out), .in1(or_1_out), .in2(slt_1_out), .in3(sllv_1_out), .in4(srlv_1_out), .in5(srav_1_out),
    .in6(add_1_out), .in7(sub_1_out), .in8(ffo_1_out), .in9(zb_1_out), .in10(bc_1_out), .in11(lui_1_out),
    .out(result), .sel(switch__S));  // open: in12, in13, in14, in15
  or or_2 (or_2_out, add_1_overflow, sub_1_overflow);
  or or_3 (or_3_out, decoder_1_out6, decoder_1_out7);
  and and_2 (signed_overflow, or_2_out, or_3_out);

  // Notes on the sheet:
  //   These are INPUTS to your circuit
  //   This is an INPUT to your circuit
  //   DO NOT CHANGE THE LOCATIONS OF THE INPUTS/OUTPUTS! IF YOU DO SO, YOU NEED TO MAKE SURE THE PINS ARE AT THE RIGHT PLACE!
  //   These are OUTPUTS to your circuit
endmodule

module \and  (
  input  [15:0] X,
  input  [15:0] Y,
  output [15:0] out
);

  assign out = X & Y;  // AND_Gate and_1, 16 bits wide
endmodule

module \or  (
  input  [15:0] X,
  input  [15:0] Y,
  output [15:0] out
);

  assign out = X | Y;  // OR_Gate or_1, 16 bits wide
endmodule

module slt (
  input  [15:0] X,
  input  [15:0] Y,
  output [15:0] out
);

  wire comparator_1_lt;

  Comparator #(.width(16)) comparator_1 (.a(X), .b(Y), .lt(comparator_1_lt));  // open: gt, eq
  assign out = {{15{1'b0}}, comparator_1_lt};  // Bit_Extender bit_extender_1
endmodule

module sllv (
  input  [15:0] X,
  input  [15:0] Y,
  output [15:0] out
);

  wire [3:0] bit_extender_1_out;
  wire [15:0] shifter_1_out;

  Bit_Extender #(.in_width(16), .out_width(4)) bit_extender_1 (.in(Y), .out(bit_extender_1_out));
  Bit_Extender #(.in_width(16), .\type ("sign")) bit_extender_2 (.in(shifter_1_out), .out(out));
  Shifter #(.width(16)) shifter_1 (.in(X), .\dist (bit_extender_1_out), .out(shifter_1_out));
endmodule

module srlv (
  input  [15:0] X,
  input  [15:0] Y,
  output [15:0] out
);

  wire [3:0] bit_extender_1_out;
  wire [15:0] shifter_1_out;

  Bit_Extender #(.in_width(16), .out_width(4)) bit_extender_1 (.in(Y), .out(bit_extender_1_out));
  Bit_Extender #(.in_width(16)) bit_extender_2 (.in(shifter_1_out), .out(out));
  Shifter #(.width(16), .shift("lr")) shifter_1 (.in(X), .\dist (bit_extender_1_out), .out(shifter_1_out));
endmodule

module srav (
  input  [15:0] X,
  input  [15:0] Y,
  output [15:0] out
);

  wire [3:0] bit_extender_1_out;

  Bit_Extender #(.in_width(16), .out_width(4)) bit_extender_1 (.in(Y), .out(bit_extender_1_out));
  Shifter #(.width(16), .shift("ar")) shifter_1 (.in(X), .\dist (bit_extender_1_out), .out(out));
endmodule

module add (
  input  [15:0] X,
  input  [15:0] Y,
  output [15:0] out,
  output overflow
);

  Adder #(.width(16)) adder_1 (.a(X), .b(Y), .out(out), .cout(overflow));  // open: cin
endmodule

module sub (
  input  [15:0] X,
  input  [15:0] Y,
  output [15:0] out,
  output overflow
);

  Subtractor #(.width(16)) subtractor_1 (.a(X), .b(Y), .out(out), .bout(overflow));  // open: bin
endmodule

module ffo (
  input  [15:0] X,
  output [15:0] out
);

  wire [3:0] bitfinder_1_index, subtractor_1_out;

  BitFinder #(.width(16), .\type ("high1")) bitfinder_1 (.in(X), .index(bitfinder_1_index));  // open: found
  Subtractor #(.width(4)) subtractor_1 (.a(4'b1111), .b(bitfinder_1_index), .out(subtractor_1_out));  // open: bin, bout
  assign out = {{12{1'b0}}, subtractor_1_out};  // Bit_Extender bit_extender_1
endmodule

module zb (
  input  [15:0] X,
  output [15:0] out
);

  wire bitfinder_1_found, bitfinder_2_found, bitfinder_3_found, bitfinder_4_found, bitfinder_5_found,
       bitfinder_6_found, bitfinder_7_found, bitfinder_8_found, bitfinder_9_found, or_1_out;

  BitFinder bitfinder_1 (.in(X[7:0]), .found(bitfinder_1_found));  // open: index
  BitFinder bitfinder_2 (.in(X[8:1]), .found(bitfinder_2_found));  // open: index
  BitFinder bitfinder_3 (.in(X[9:2]), .found(bitfinder_3_found));  // open: index
  BitFinder bitfinder_4 (.in(X[10:3]), .found(bitfinder_4_found));  // open: index
  BitFinder bitfinder_5 (.in(X[11:4]), .found(bitfinder_5_found));  // open: index
  BitFinder bitfinder_6 (.in(X[12:5]), .found(bitfinder_6_found));  // open: index
  BitFinder bitfinder_7 (.in(X[13:6]), .found(bitfinder_7_found));  // open: index
  BitFinder bitfinder_8 (.in(X[14:7]), .found(bitfinder_8_found));  // open: index
  BitFinder bitfinder_9 (.in(X[15:8]), .found(bitfinder_9_found));  // open: index
  or or_1 (or_1_out, bitfinder_1_found, bitfinder_2_found, bitfinder_3_found, bitfinder_4_found, bitfinder_5_found, bitfinder_6_found, bitfinder_7_found, bitfinder_8_found, bitfinder_9_found);
  assign out = {{15{1'b0}}, or_1_out};  // Bit_Extender bit_extender_1
endmodule

module bc (
  input  [15:0] X,
  output [15:0] out
);

  wire [4:0] bitadder_1_out;

  BitAdder #(.width(16)) bitadder_1 (.in0(X), .out(bitadder_1_out));
  assign out = {{11{1'b0}}, bitadder_1_out};  // Bit_Extender bit_extender_1
endmodule

module lui (
  input  [15:0] X,
  output [15:0] out
);

  wire [15:0] shifter_1_out;

  Bit_Extender #(.in_width(16)) bit_extender_1 (.in(shifter_1_out), .out(out));
  Shifter #(.width(16)) shifter_1 (.in(X), .\dist (4'b1000), .out(shifter_1_out));
endmodule
