// Logisim project cpu.circ as structural Verilog: 4 circuits, main circuit main
module main (
  input  [15:0] From_Instr_Mem,
  input  clk,
  output [15:0] r0,
  output [15:0] r1,
  output [15:0] r2,
  output [15:0] r3,
  output [15:0] Display_0,
  output [15:0] Display_1,
  output [15:0] To_Instr_Mem,
  output [15:0] Data_Mem_Data,
  output [15:0] Data_Mem_Addr,
  output Data_Mem_Write
);

  wire and_2_out, and_3_out, Br, control_1_alusrc, control_1_disp, control_1_jr, control_1_link,
       control_1_memtoreg, control_1_regdst, control_1_regwrite, J, main_2_equal, not_1_out, not_2_out,
       or_1_out, xor_1_out;
  wire [1:0] control_1_branch, multiplexer_2_out, multiplexer_3_out;
  wire [2:0] control_1_aluop;
  wire [3:0] alu_control_1_switch;
  wire [15:0] Add_2_result, Add_result, bit_extender_1_out, datamem_1_readdata, main_1_read_data_1,
       multiplexer_1_out, multiplexer_4_out, multiplexer_5_out, multiplexer_6_out, multiplexer_7_out,
       multiplexer_8_out, multiplexer_9_out, register_2_q;

  Hex_Digit_Display hex_digit_display_1 (.value(From_Instr_Mem[15:12]));  // open: dp
  Hex_Digit_Display hex_digit_display_2 (.value(register_2_q[15:12]));  // open: dp
  Register #(.width(16)) register_1 (.D(multiplexer_7_out), .Q(To_Instr_Mem), .clk(clk));  // open: en, clr
  Hex_Digit_Display hex_digit_display_3 (.value(From_Instr_Mem[11:8]));  // open: dp
  Hex_Digit_Display hex_digit_display_4 (.value(From_Instr_Mem[7:4]));  // open: dp
  Hex_Digit_Display hex_digit_display_5 (.value(register_2_q[7:4]));  // open: dp
  Hex_Digit_Display hex_digit_display_6 (.value(register_2_q[11:8]));  // open: dp
  alu_main Add (.switch__S(4'b0110), .X(To_Instr_Mem), .result(Add_result), .Y(16'h1));  // open: equal, signed_overflow
  or or_1 (or_1_out, Br, J);
  Hex_Digit_Display hex_digit_display_7 (.value(From_Instr_Mem[3:0]));  // open: dp
  Hex_Digit_Display hex_digit_display_8 (.value(register_2_q[3:0]));  // open: dp
  Multiplexer #(.width(16), .enable("false")) multiplexer_1 (
    .in0(From_Instr_Mem), .in1({16{1'b0}}), .out(multiplexer_1_out), .sel(or_1_out));
  Register #(.width(16)) register_2 (.D(multiplexer_1_out), .Q(register_2_q), .clk(clk));  // open: en, clr
  Hex_Digit_Display hex_digit_display_9 (.value(Display_0[15:12]));  // open: dp
  Hex_Digit_Display hex_digit_display_10 (.value(Display_0[11:8]));  // open: dp
  Multiplexer #(.width(2), .enable("false")) multiplexer_2 (
    .in0(register_2_q[9:8]), .in1(register_2_q[7:6]), .out(multiplexer_2_out), .sel(control_1_regdst));
  Multiplexer #(.width(2), .enable("false")) multiplexer_3 (
    .in0(multiplexer_2_out), .in1(2'b11), .out(multiplexer_3_out), .sel(control_1_link));
  Hex_Digit_Display hex_digit_display_11 (.value(Display_0[3:0]));  // open: dp
  Hex_Digit_Display hex_digit_display_12 (.value(Display_0[7:4]));  // open: dp
  Control control_1 (
    .Instruction(register_2_q[15:12]), .Jump(J), .Branch(control_1_branch), .Disp(control_1_disp),
    .MemToReg(control_1_memtoreg), .ALUOp(control_1_aluop), .MemWrite(Data_Mem_Write),
    .ALUSrc(control_1_alusrc), .RegDst(control_1_regdst), .RegWrite(control_1_regwrite),
    .Link(control_1_link), .JR(control_1_jr));
  Hex_Digit_Display hex_digit_display_13 (.value(Display_1[15:12]));  // open: dp
  alu_main Add_2 (
    .switch__S(4'b0110), .X(Add_result), .result(Add_2_result), .Y(bit_extender_1_out));  // open: equal, signed_overflow
  Regfile_main main_1 (
    .Read_register_1(register_2_q[11:10]), .Read_register_2(register_2_q[9:8]),
    .write_register(multiplexer_3_out), .write_data(multiplexer_9_out), .Reg_0_Value(r0), .Reg_1_Value(r1),
    .Reg_2_Value(r2), .Reg_3_Value(r3), .RegWrite(control_1_regwrite), .clock(clk),
    .Read_Data_1(main_1_read_data_1), .Read_Data_2(Data_Mem_Data));
  assign bit_extender_1_out = {{8{register_2_q[7]}}, register_2_q[7:0]};  // Bit_Extender bit_extender_1
  Hex_Digit_Display hex_digit_display_14 (.value(Display_1[11:8]));  // open: dp
  Hex_Digit_Display hex_digit_display_15 (.value(Display_1[7:4]));  // open: dp
  Multiplexer #(.width(16), .enable("false")) multiplexer_4 (
    .in0(Add_result), .in1(Add_2_result), .out(multiplexer_4_out), .sel(Br));
  and and_1 (Br, xor_1_out, control_1_branch[0]);
  Multiplexer #(.width(16), .enable("false")) multiplexer_5 (
    .in0(Data_Mem_Data), .in1(bit_extender_1_out), .out(multiplexer_5_out), .sel(control_1_alusrc));
  ALU_Control alu_control_1 (.ALUOp(control_1_aluop), .funct(register_2_q[5:0]), .switch(alu_control_1_switch));
  Hex_Digit_Display hex_digit_display_16 (.value(Display_1[3:0]));  // open: dp
  xor xor_1 (xor_1_out, control_1_branch[1], main_2_equal);
  alu_main main_2 (
    .switch__S(alu_control_1_switch), .X(main_1_read_data_1), .equal(main_2_equal), .result(Data_Mem_Addr),
    .Y(multiplexer_5_out));  // open: signed_overflow
  Multiplexer #(.width(16), .enable("false")) multiplexer_6 (
    .in0(multiplexer_4_out), .in1({Add_result[15:12], register_2_q[11:0]}), .out(multiplexer_6_out), .sel(J));
  Multiplexer #(.width(16), .enable("false")) multiplexer_7 (
    .in0(multiplexer_6_out), .in1(main_1_read_data_1), .out(multiplexer_7_out), .sel(control_1_jr));
  DataMem datamem_1 (
    .Address(Data_Mem_Addr), .WriteData(Data_Mem_Data), .ReadData(datamem_1_readdata),
    .MemWrite(Data_Mem_Write), .clk(clk));  // open: reset
  not not_1 (not_1_out, control_1_link);
  Multiplexer #(.width(16), .enable("false")) multiplexer_8 (
    .in0(Data_Mem_Addr), .in1(datamem_1_readdata), .out(multiplexer_8_out), .sel(control_1_memtoreg));
  and and_2 (and_2_out, control_1_disp, not_2_out);
  Multiplexer #(.width(16), .enable("false")) multiplexer_9 (
    .in0(Add_result), .in1(multiplexer_8_out), .out(multiplexer_9_out), .sel(not_1_out));
  and and_3 (and_3_out, control_1_disp, register_2_q[0]);
  Register #(.width(16)) register_3 (.D(main_1_read_data_1), .en(and_2_out), .Q(Display_0), .clk(clk));  // open: clr
  not not_2 (not_2_out, register_2_q[0]);
  Register #(.width(16)) register_4 (.D(main_1_read_data_1), .en(and_3_out), .Q(Display_1), .clk(clk));  // open: clr

  // Other names for the same wires on the sheet: d0[15:0] = Display_0; d1[15:0] = Display_1;
  //   MemWrite = Data_Mem_Write

  // Notes on the sheet:
  //   This is the current PC that you need to send as OUTPUT
  //   This is the instruction that you would receive as INPUT
  //   DO NOT CHANGE THE LOCATIONS OF THE INPUTS/OUTPUTS! IF YOU DO SO, YOU NEED TO MAKE SURE THE PINS ARE AT THE RIGHT PLACE!
  //   This is a CLK that is an INPUT driven from the harness.
  //   Remember, this circuit is loaded from the harness to be tested!
  //   These are OUTPUTS to the circuit
  //   These are OUTPUTS to the circuit
endmodule

module Control (
  input  [3:0] Instruction,
  output RegDst,
  output Jump,
  output Disp,
  output MemToReg,
  output MemWrite,
  output ALUSrc,
  output RegWrite,
  output [2:0] ALUOp,
  output Link,
  output JR,
  output [1:0] Branch
);

  wire Add_out, And_out, bc_out, decoder_1_out0, decoder_1_out1, decoder_1_out2, decoder_1_out3,
       decoder_1_out4, decoder_1_out5, decoder_1_out6, decoder_1_out8, decoder_1_out10, decoder_1_out12,
       decoder_1_out13, decoder_1_out14, decoder_1_out15, ffo_out, lui_out, or_9_out, or_10_out, Or_11_out,
       zb_out;

  Decoder #(.select(4), .enable("false")) decoder_1 (
    .out0(decoder_1_out0), .out1(decoder_1_out1), .out2(decoder_1_out2), .out3(decoder_1_out3),
    .out4(decoder_1_out4), .out5(decoder_1_out5), .out6(decoder_1_out6), .out7(Link), .out8(decoder_1_out8),
    .out9(JR), .out10(decoder_1_out10), .out11(Branch[1]), .out12(decoder_1_out12), .out13(decoder_1_out13),
    .out14(decoder_1_out14), .out15(decoder_1_out15), .sel(Instruction));
  buf or_1 (RegDst, decoder_1_out0);  // OR_Gate
  or or_2 (Branch[0], Branch[1], decoder_1_out10);
  or or_3 (Jump, Link, decoder_1_out8, JR);
  buf or_4 (Disp, decoder_1_out15);  // OR_Gate
  buf or_5 (MemToReg, decoder_1_out14);  // OR_Gate
  buf or_6 (MemWrite, decoder_1_out12);  // OR_Gate
  or or_7 (ALUSrc, decoder_1_out4, decoder_1_out5, decoder_1_out6, decoder_1_out12, decoder_1_out13, decoder_1_out14, decoder_1_out15);
  or or_8 (RegWrite, or_10_out, or_9_out);
  or or_9 (or_9_out, decoder_1_out5, decoder_1_out6, Link, decoder_1_out13, decoder_1_out14);
  or or_10 (or_10_out, decoder_1_out0, decoder_1_out1, decoder_1_out2, decoder_1_out3, decoder_1_out4);
  buf ffo (ffo_out, decoder_1_out1);
  buf zb (zb_out, decoder_1_out2);
  buf bc (bc_out, decoder_1_out3);
  buf lui (lui_out, decoder_1_out13);
  buf And (And_out, decoder_1_out5);
  or Add (Add_out, decoder_1_out4, decoder_1_out12, decoder_1_out14);
  buf Or_11 (Or_11_out, decoder_1_out6);
  or _0 (ALUOp[0], Add_out, Or_11_out, zb_out, lui_out);
  or _1 (ALUOp[1], And_out, Or_11_out, bc_out, lui_out);
  or _2 (ALUOp[2], ffo_out, zb_out, bc_out, lui_out);
endmodule

module ALU_Control (
  input  [2:0] ALUOp,
  input  [5:0] funct,
  output [3:0] switch
);

  wire decoder_1_out0, decoder_1_out1, decoder_1_out3, decoder_1_out4, decoder_1_out5, decoder_1_out6,
       decoder_1_out7;
  wire [3:0] _0_out, bit_extender_1_out;

  Bit_Extender #(.in_width(6), .out_width(4)) bit_extender_1 (.in(funct), .out(bit_extender_1_out));
  Decoder #(.select(3), .enable("false")) decoder_1 (
    .out0(decoder_1_out0), .out1(decoder_1_out1), .out3(decoder_1_out3), .out4(decoder_1_out4),
    .out5(decoder_1_out5), .out6(decoder_1_out6), .out7(decoder_1_out7), .sel(ALUOp));  // open: out2
  or _3 (_0_out[3], decoder_1_out4, decoder_1_out5, decoder_1_out6, decoder_1_out7);
  buf _2 (_0_out[2], decoder_1_out1);  // OR_Gate
  Multiplexer #(.width(4), .enable("false")) multiplexer_1 (
    .in0(_0_out), .in1(bit_extender_1_out), .out(switch), .sel(decoder_1_out0));
  or _1 (_0_out[1], decoder_1_out1, decoder_1_out6, decoder_1_out7);
  or _0 (_0_out[0], decoder_1_out3, decoder_1_out5, decoder_1_out7);
endmodule

// Data Memory
module DataMem (
  input  MemWrite,
  input  [15:0] Address,
  input  [15:0] WriteData,
  input  reset,
  input  clk,
  output [15:0] ReadData
);

  wire not_1_out;

  not not_1 (not_1_out, MemWrite);
  assign ReadData = MemWrite ? WriteData : 16'bz;  // Controlled_Buffer controlled_buffer_1
  RAM #(.addrWidth(16), .dataWidth(16)) ram_1 (
    .addr(Address), .data(ReadData), .sel(1'b1), .clk(clk), .ld(not_1_out), .clr(reset));
endmodule
